// Logisim project LC-2200-16.circ as structural Verilog: 5 circuits, main circuit LC2200 Datapath
module LC2200_Datapath (
);

  wire CLK, comparator_1_eq, DrALU, DrMEM, DrOFF, DrPC, DrREG, LdA, LdB, LdIR, LdMAR, LdPC, LdZ, RESET,
       WrMEM, WrREG, Z;
  wire [1:0] func, microcontroller_1_regsello;
  wire [2:0] OP;
  wire [3:0] bit_extender_1_out, controlled_buffer_1_out, controlled_buffer_1_out_2,
       controlled_buffer_1_out_4, regno, RX, RY;
  wire [4:0] OFFSET;
  wire [11:8] controlled_buffer_1_out_3;
  wire [15:0] A_q, alu_1_out, B_q, bit_extender_2_out, MAR_q, PC_q, ram_1_dout, Registers_dout;

  Hex_Digit_Display hex_digit_display_1 (.value(controlled_buffer_1_out_4));  // open: dp
  Hex_Digit_Display hex_digit_display_2 (.value(controlled_buffer_1_out_3));  // open: dp
  Hex_Digit_Display hex_digit_display_3 (.value(controlled_buffer_1_out_2));  // open: dp
  Button u_RESET (.out(RESET));
  Clock u_CLK (.out(CLK));
  Hex_Digit_Display hex_digit_display_4 (.value(controlled_buffer_1_out));  // open: dp
  assign bit_extender_1_out = {{1{1'b0}}, OP};  // Bit_Extender bit_extender_1
  Register #(.width(16)) PC (
    .D({controlled_buffer_1_out_4, controlled_buffer_1_out_3, controlled_buffer_1_out_2, controlled_buffer_1_out}),
    .en(LdPC), .Q(PC_q), .clk(CLK), .clr(RESET));
  assign {controlled_buffer_1_out_4, controlled_buffer_1_out_3, controlled_buffer_1_out_2, controlled_buffer_1_out} = DrPC ? PC_q : 16'bz;  // Controlled_Buffer controlled_buffer_1
  Comparator #(.width(16), .mode("unsigned")) comparator_1 (
    .a({controlled_buffer_1_out_4, controlled_buffer_1_out_3, controlled_buffer_1_out_2, controlled_buffer_1_out}),
    .b({16{1'b0}}), .eq(comparator_1_eq));  // open: gt, lt
  Hex_Digit_Display hex_digit_display_5 (.value(RX));  // open: dp
  Hex_Digit_Display hex_digit_display_6 (.value(bit_extender_1_out));  // open: dp
  Register #(.width(16)) A (
    .D({controlled_buffer_1_out_4, controlled_buffer_1_out_3, controlled_buffer_1_out_2, controlled_buffer_1_out}),
    .en(LdA), .Q(A_q), .clk(CLK));  // open: clr
  Register #(.width(1)) u_Z (.D(comparator_1_eq), .en(LdZ), .Q(Z), .clk(CLK));  // open: clr
  Hex_Digit_Display hex_digit_display_7 (.value(OFFSET[4:1]));  // open: dp
  Hex_Digit_Display hex_digit_display_8 (.value(RY));  // open: dp
  ALU alu_1 (.func(func), .A(A_q), .B(B_q), .OUT(alu_1_out));
  assign {controlled_buffer_1_out_4, controlled_buffer_1_out_3, controlled_buffer_1_out_2, controlled_buffer_1_out} = DrALU ? alu_1_out : 16'bz;  // Controlled_Buffer controlled_buffer_2
  Register #(.width(16)) B (
    .D({controlled_buffer_1_out_4, controlled_buffer_1_out_3, controlled_buffer_1_out_2, controlled_buffer_1_out}),
    .en(LdB), .Q(B_q), .clk(CLK));  // open: clr
  // Probe on OFFSET
  Registers Registers (
    .WrREG(WrREG), .regno(regno), .CLK(CLK),
    .Din({controlled_buffer_1_out_4, controlled_buffer_1_out_3, controlled_buffer_1_out_2, controlled_buffer_1_out}),
    .Dout(Registers_dout));
  assign {controlled_buffer_1_out_4, controlled_buffer_1_out_3, controlled_buffer_1_out_2, controlled_buffer_1_out} = DrREG ? Registers_dout : 16'bz;  // Controlled_Buffer controlled_buffer_3
  Register #(.width(16)) MAR (
    .D({controlled_buffer_1_out_4, controlled_buffer_1_out_3, controlled_buffer_1_out_2, controlled_buffer_1_out}),
    .en(LdMAR), .Q(MAR_q), .clk(CLK), .clr(RESET));
  RAM ram_1 (
    .WrMEM(WrMEM), .CLK(CLK), .Addr(MAR_q),
    .Din({controlled_buffer_1_out_4, controlled_buffer_1_out_3, controlled_buffer_1_out_2, controlled_buffer_1_out}),
    .Dout(ram_1_dout));
  assign {controlled_buffer_1_out_4, controlled_buffer_1_out_3, controlled_buffer_1_out_2, controlled_buffer_1_out} = DrMEM ? ram_1_dout : 16'bz;  // Controlled_Buffer controlled_buffer_4
  Multiplexer #(.select(2), .width(4), .disabled(0), .enable("false")) multiplexer_1 (
    .in0(RX), .in1(RY), .in2(OFFSET[4:1]), .out(regno), .sel(microcontroller_1_regsello));  // open: in3
  Microcontroller microcontroller_1 (
    .LdMAR(LdMAR), .LdIR(LdIR), .LdPC(LdPC), .DrOFF(DrOFF), .DrPC(DrPC), .DrALU(DrALU), .DrMEM(DrMEM),
    .DrREG(DrREG), .LdA(LdA), .LdB(LdB), .LdZ(LdZ), .WrREG(WrREG), .WrMEM(WrMEM),
    .RegSelLo(microcontroller_1_regsello[0]), .RegSelHi(microcontroller_1_regsello[1]), .ALULo(func[0]),
    .ALUHi(func[1]), .IR(OP), .Z(Z), .RESET(RESET), .CLK(CLK));
  Register #(.width(16)) IR (
    .D({controlled_buffer_1_out_4, controlled_buffer_1_out_3, controlled_buffer_1_out_2, controlled_buffer_1_out}),
    .en(LdIR), .Q({OP, RX, RY, OFFSET}), .clk(CLK));  // open: clr
  Hex_Digit_Display hex_digit_display_9 (.value(regno));  // open: dp
  assign bit_extender_2_out = {{11{OFFSET[4]}}, OFFSET};  // Bit_Extender bit_extender_2
  assign {controlled_buffer_1_out_4, controlled_buffer_1_out_3, controlled_buffer_1_out_2, controlled_buffer_1_out} = DrOFF ? bit_extender_2_out : 16'bz;  // Controlled_Buffer controlled_buffer_5

  // Other names for the same wires on the sheet: RZ[3:0] = OFFSET[4:1]
endmodule

module ALU (
  input  [15:0] A,
  input  [15:0] B,
  input  [1:0] func,
  output [15:0] OUT
);

  wire [15:0] ADD, NAND, plus_1, SUB;

  Adder #(.width(16)) adder_1 (.a(A), .b(B), .out(ADD));  // open: cin, cout
  Subtractor #(.width(16)) subtractor_1 (.a(A), .b(B), .out(SUB));  // open: bin, bout
  Multiplexer #(.select(2), .width(16), .disabled(0), .enable("false")) multiplexer_1 (
    .in0(ADD), .in1(NAND), .in2(SUB), .in3(plus_1), .out(OUT), .sel(func));
  assign NAND = ~(A & B);  // NAND_Gate nand_1, 16 bits wide
  Adder #(.width(16)) adder_2 (.a(A), .b(16'h1), .out(plus_1));  // open: cin, cout
endmodule

module Registers (
  input  [15:0] Din,
  input  WrREG,
  input  [3:0] regno,
  input  CLK,
  output [15:0] Dout
);

  wire demultiplexer_1_out1, demultiplexer_1_out2, demultiplexer_1_out3, demultiplexer_1_out4,
       demultiplexer_1_out5, demultiplexer_1_out6, demultiplexer_1_out7, demultiplexer_1_out8,
       demultiplexer_1_out9, demultiplexer_1_out10, demultiplexer_1_out11, demultiplexer_1_out12,
       demultiplexer_1_out13, demultiplexer_1_out14, demultiplexer_1_out15;
  wire [15:0] register_1_q, register_2_q, register_3_q, register_4_q, register_5_q, register_6_q,
       register_7_q, register_8_q, register_9_q, register_10_q, register_11_q, register_12_q, register_13_q,
       register_14_q, register_15_q;

  Demultiplexer #(.select(4), .disabled(0), .enable("false")) demultiplexer_1 (
    .out1(demultiplexer_1_out1), .out2(demultiplexer_1_out2), .out3(demultiplexer_1_out3),
    .out4(demultiplexer_1_out4), .out5(demultiplexer_1_out5), .out6(demultiplexer_1_out6),
    .out7(demultiplexer_1_out7), .out8(demultiplexer_1_out8), .out9(demultiplexer_1_out9),
    .out10(demultiplexer_1_out10), .out11(demultiplexer_1_out11), .out12(demultiplexer_1_out12),
    .out13(demultiplexer_1_out13), .out14(demultiplexer_1_out14), .out15(demultiplexer_1_out15), .in(WrREG),
    .sel(regno));  // open: out0
  Register #(.width(16)) register_1 (.D(Din), .en(demultiplexer_1_out4), .Q(register_1_q), .clk(CLK));  // open: clr
  Register #(.width(16)) register_2 (.D(Din), .en(demultiplexer_1_out8), .Q(register_2_q), .clk(CLK));  // open: clr
  Register #(.width(16)) register_3 (.D(Din), .en(demultiplexer_1_out12), .Q(register_3_q), .clk(CLK));  // open: clr
  Register #(.width(16)) register_4 (.D(Din), .en(demultiplexer_1_out1), .Q(register_4_q), .clk(CLK));  // open: clr
  Register #(.width(16)) register_5 (.D(Din), .en(demultiplexer_1_out5), .Q(register_5_q), .clk(CLK));  // open: clr
  Register #(.width(16)) register_6 (.D(Din), .en(demultiplexer_1_out9), .Q(register_6_q), .clk(CLK));  // open: clr
  Register #(.width(16)) register_7 (.D(Din), .en(demultiplexer_1_out13), .Q(register_7_q), .clk(CLK));  // open: clr
  Register #(.width(16)) register_8 (.D(Din), .en(demultiplexer_1_out2), .Q(register_8_q), .clk(CLK));  // open: clr
  Register #(.width(16)) register_9 (.D(Din), .en(demultiplexer_1_out6), .Q(register_9_q), .clk(CLK));  // open: clr
  Register #(.width(16)) register_10 (.D(Din), .en(demultiplexer_1_out10), .Q(register_10_q), .clk(CLK));  // open: clr
  Register #(.width(16)) register_11 (.D(Din), .en(demultiplexer_1_out14), .Q(register_11_q), .clk(CLK));  // open: clr
  Register #(.width(16)) register_12 (.D(Din), .en(demultiplexer_1_out3), .Q(register_12_q), .clk(CLK));  // open: clr
  Register #(.width(16)) register_13 (.D(Din), .en(demultiplexer_1_out7), .Q(register_13_q), .clk(CLK));  // open: clr
  Register #(.width(16)) register_14 (.D(Din), .en(demultiplexer_1_out11), .Q(register_14_q), .clk(CLK));  // open: clr
  Register #(.width(16)) register_15 (.D(Din), .en(demultiplexer_1_out15), .Q(register_15_q), .clk(CLK));  // open: clr
  Multiplexer #(.select(4), .width(16), .disabled(0), .enable("false")) multiplexer_1 (
    .in0({16{1'b0}}), .in1(register_4_q), .in2(register_8_q), .in3(register_12_q), .in4(register_1_q),
    .in5(register_5_q), .in6(register_9_q), .in7(register_13_q), .in8(register_2_q), .in9(register_6_q),
    .in10(register_10_q), .in11(register_14_q), .in12(register_3_q), .in13(register_7_q),
    .in14(register_11_q), .in15(register_15_q), .out(Dout), .sel(regno));
endmodule

module RAM (
  input  [15:0] Addr,
  input  [15:0] Din,
  input  WrMEM,
  input  CLK,
  output [15:0] Dout
);

  wire not_1_out;

  RAM_part #(.addrWidth(16), .dataWidth(16)) ram_1 (
    .addr(Addr), .data(Dout), .sel(1'b1), .clk(CLK), .ld(not_1_out));  // open: clr
  not not_1 (not_1_out, WrMEM);
  assign Dout = WrMEM ? Din : 16'bz;  // Controlled_Buffer controlled_buffer_1
endmodule

module Microcontroller (
  input  [2:0] IR,
  input  Z,
  input  RESET,
  input  CLK,
  output LdA,
  output LdB,
  output LdZ,
  output WrREG,
  output WrMEM,
  output RegSelLo,
  output RegSelHi,
  output ALULo,
  output ALUHi,
  output LdMAR,
  output LdIR,
  output LdPC,
  output DrOFF,
  output DrPC,
  output DrALU,
  output DrMEM,
  output DrREG
);

  wire chkZ;
  wire [5:0] multiplexer_1_out, rom_1_data, rom_2_data, State_q;
  wire [23:0] Microstate;

  ROM #(.addrWidth(3), .dataWidth(6)) rom_1 (.addr(IR), .data(rom_1_data), .sel(1'b1));
  ROM #(.addrWidth(2), .dataWidth(6)) rom_2 (.addr({1'b0, Z}), .data(rom_2_data), .sel(1'b1));
  Multiplexer #(.select(2), .width(6), .disabled(0), .enable("false")) multiplexer_1 (
    .in0(Microstate[5:0]), .in1(rom_1_data), .in2(rom_2_data), .out(multiplexer_1_out),
    .sel({chkZ, Microstate[23]}));  // open: in3
  Register #(.width(6)) State (.D(multiplexer_1_out), .en(1'b1), .Q(State_q), .clk(CLK), .clr(RESET));
  ROM #(.addrWidth(6), .dataWidth(25)) rom_3 (
    .addr(State_q),
    .data({chkZ, Microstate[23], ALUHi, ALULo, RegSelHi, RegSelLo, WrMEM, WrREG, LdZ, LdB, LdA, LdMAR, LdIR, LdPC, DrOFF, DrPC, DrALU, DrMEM, DrREG, Microstate[5:0]}),
    .sel(1'b1));

  // Other names for the same wires on the sheet: Microstate (some bits) = {chkZ, ALUHi, ALULo, RegSelHi, RegSelLo, WrMEM, WrREG, LdZ, LdB, LdA, LdMAR, LdIR, LdPC, DrOFF, DrPC, DrALU, DrMEM, DrREG};
  //   OPTest = Microstate[23]; Next_State[5:0] = Microstate[5:0]; OP[2:0] = IR

  // Notes on the sheet:
  //   contents of rom_1 (hex, n*v repeats v):
  //   3 9 6 c 10 14 1b 1d
  //   contents of rom_2 (hex, n*v repeats v):
  //   0 18
  //   contents of rom_3 (hex, n*v repeats v):
  //   6201 1082 e00900 84044 108045 20100 84047 8408 20100 8404a 10804b 220100 8404d 840e 210f 20080 84051
  //   8412 2113 40040 4055 88056 410117 1000000 4219 841a 900 a021c 840 1d
endmodule
